// Logisim project TFCircuitos.circ as structural Verilog: 7 circuits, main circuit main
module main (
  input  B3,
  input  B2,
  input  B1,
  input  B0,
  input  B3_1,
  input  B2_1,
  input  B1_1,
  input  B0_1,
  input  T_B3,
  input  T_B2,
  input  T_B1,
  input  T_B0,
  input  Tiro,
  output Led_Verde,
  output Led_Vermelho
);

  wire codificador_1_sab3, codificador_1_sbb2, codificador_1_scb1, codificador_1_sdb0, comparador_1_acerto,
       comparador_1_erro, comparador_2_acerto, comparador_2_erro;

  Codificador codificador_1 (
    .A(T_B3), .B(T_B2), .C(T_B1), .D(T_B0), .SaB3(codificador_1_sab3), .SbB2(codificador_1_sbb2),
    .ScB1(codificador_1_scb1), .SdB0(codificador_1_sdb0));
  Comparador comparador_1 (
    .B3(B3), .B2(B2), .B1(B1), .B0(B0), .T3(codificador_1_sab3), .T2(codificador_1_sbb2),
    .T1(codificador_1_scb1), .T0(codificador_1_sdb0), .Tiro(Tiro), .Acerto(comparador_1_acerto),
    .Erro(comparador_1_erro));
  Comparador comparador_2 (
    .B3(B3_1), .B2(B2_1), .B1(B1_1), .B0(B0_1), .T3(codificador_1_sab3), .T2(codificador_1_sbb2),
    .T1(codificador_1_scb1), .T0(codificador_1_sdb0), .Tiro(Tiro), .Acerto(comparador_2_acerto),
    .Erro(comparador_2_erro));
  or or_1 (Led_Verde, comparador_1_acerto, comparador_2_acerto);
  and and_1 (Led_Vermelho, comparador_1_erro, comparador_2_erro);

  // Notes on the sheet:
  //   Barco 1
  //   Barco 2
  //   Tiro 
endmodule

module Sa (
  input  A,
  input  B,
  input  C,
  input  D,
  output B3
);

  wire and_1_out, and_2_out, and_3_out, and_4_out, and_5_out;

  and and_1 (and_1_out, A, ~D);  // AND_Gate
  and and_2 (and_2_out, ~B, ~C, ~D);  // AND_Gate
  and and_3 (and_3_out, B, C, ~D);  // AND_Gate
  and and_4 (and_4_out, ~A, ~B, C, D);  // AND_Gate
  and and_5 (and_5_out, ~A, B, ~C, D);  // AND_Gate
  or or_1 (B3, and_1_out, and_2_out, and_3_out, and_4_out, and_5_out);
endmodule

module Sb (
  input  A,
  input  B,
  input  C,
  input  D,
  output B2
);

  wire and_1_out, and_2_out, and_3_out, and_4_out;

  and and_1 (and_1_out, ~A, C);  // AND_Gate
  and and_2 (and_2_out, ~B, C);  // AND_Gate
  and and_3 (and_3_out, C, ~D);  // AND_Gate
  and and_4 (and_4_out, ~A, ~B, D);  // AND_Gate
  or or_1 (B2, and_1_out, and_2_out, and_3_out, and_4_out);
endmodule

module Sc (
  input  A,
  input  B,
  input  C,
  input  D,
  output B1
);

  wire and_1_out, and_2_out, and_3_out;

  and and_1 (and_1_out, ~A, ~D);  // AND_Gate
  and and_2 (and_2_out, ~B, ~D);  // AND_Gate
  and and_3 (and_3_out, A, C, D);
  or or_1 (B1, and_1_out, and_2_out, and_3_out);
endmodule

module Sd (
  input  A,
  input  B,
  input  C,
  input  D,
  output B0
);

  wire and_1_out, and_2_out, and_3_out, and_4_out;

  and and_1 (and_1_out, ~B, C, ~D);  // AND_Gate
  and and_2 (and_2_out, A, ~C, ~D);  // AND_Gate
  and and_3 (and_3_out, ~A, C, D);  // AND_Gate
  and and_4 (and_4_out, A, B, D);
  or or_1 (B0, and_1_out, and_2_out, and_3_out, and_4_out);
endmodule

module Codificador (
  input  A,
  input  B,
  input  C,
  input  D,
  output SaB3,
  output SbB2,
  output ScB1,
  output SdB0
);

  Sa sa_1 (.A(A), .B(B), .C(C), .D(D), .B3(SaB3));
  Sb sb_1 (.A(A), .B(B), .C(C), .D(D), .B2(SbB2));
  Sc sc_1 (.A(A), .B(B), .C(C), .D(D), .B1(ScB1));
  Sd sd_1 (.A(A), .B(B), .C(C), .D(D), .B0(SdB0));
endmodule

module Comparador (
  input  B3,
  input  B2,
  input  B1,
  input  B0,
  input  T3,
  input  T2,
  input  T1,
  input  T0,
  input  Tiro,
  output Acerto,
  output Erro
);

  wire not_1_out, not_2_out, not_3_out, not_4_out, xor_1_out, xor_2_out, xor_3_out, xor_4_out;

  xor xor_1 (xor_1_out, B3, T3);
  not not_1 (not_1_out, xor_1_out);
  xor xor_2 (xor_2_out, B2, T2);
  not not_2 (not_2_out, xor_2_out);
  xor xor_3 (xor_3_out, B1, T1);
  not not_3 (not_3_out, xor_3_out);
  xor xor_4 (xor_4_out, B0, T0);
  not not_4 (not_4_out, xor_4_out);
  and and_1 (Acerto, not_1_out, not_2_out, not_3_out, not_4_out, Tiro);
  and and_2 (Erro, ~Acerto, Tiro);  // AND_Gate
endmodule
